# Fritzing sketch Alfombra-esquema (saved by Fritzing 0.9.3b)
breadboards: 2

parts:
  LCD1 = LCD screen
  R1 = Resistor [tolerance=±5% resistance=3.3k package=THT]
  U1 = ESP 32 DEVKIT DOIT
  J1 = Piezo Speaker
  LED1 = LED - 3mm [color="Red (633nm)" package="3 mm [THT]"]
  LED2 = LED - 3mm [color="Yellow (592nm)" package="3 mm [THT]"]
  R2 = Resistor [tolerance=±5% resistance=470 package=THT]
  R3 = Resistor [tolerance=±5% resistance=470 package=THT]

nets:
  N1: LCD1.VSS, LCD1.R/W, LCD1.LED-, R1.Pin_0, J1.pin1, LED1.cathode, LED2.cathode
  N2: LCD1.VDD, LCD1.LED+
  N3: LCD1.V0, R1.Pin_1
  N4: LCD1.RS, U1.D19
  N5: LCD1.E, U1.D23
  N6: LCD1.DB4, U1.D26
  N7: LCD1.DB5, U1.D32
  N8: LCD1.DB6, LCD1.DB7, U1.D22, U1.D18, U1.TX2, U1.RX2, U1.D4, U1.D15, U1.3V3, R2.Pin_1, R3.Pin_1
  N9: U1.D25, J1.pin2
  N10: LED1.anode, R2.Pin_0
  N11: LED2.anode, R3.Pin_0
